// Logisim project alu.circ as structural Verilog
// 1-bit Half\nAdder
module _1_bit_half_adder (
  input  A_In,
  input  B_In,
  output Sum_Out,
  output Carry_Out
);

  xor xor_1 (Sum_Out, A_In, B_In);
  and and_1 (Carry_Out, A_In, B_In);
endmodule

// 4 Bit Full Adder
module _4_bit_full_adder (
  input  A3,
  input  A2,
  input  A1,
  input  A0,
  input  B3,
  input  B2,
  input  B1,
  input  B0,
  input  Carry_In,
  output Carry_Out,
  output S3,
  output S2,
  output S1,
  output S0
);

  wire n1_bit_full_adder_2_carry_out, n1_bit_full_adder_3_carry_out, n1_bit_full_adder_4_carry_out;

  _1_bit_full_adder u_1_bit_full_adder_1 (
    .Carry_In(n1_bit_full_adder_2_carry_out), .A_In(A3), .B_In(B3), .Sum_Out(S3), .Carry_Out(Carry_Out));
  _1_bit_full_adder u_1_bit_full_adder_2 (
    .Carry_In(n1_bit_full_adder_3_carry_out), .A_In(A2), .B_In(B2), .Sum_Out(S2),
    .Carry_Out(n1_bit_full_adder_2_carry_out));
  _1_bit_full_adder u_1_bit_full_adder_3 (
    .Carry_In(n1_bit_full_adder_4_carry_out), .A_In(A1), .B_In(B1), .Sum_Out(S1),
    .Carry_Out(n1_bit_full_adder_3_carry_out));
  _1_bit_full_adder u_1_bit_full_adder_4 (
    .Carry_In(Carry_In), .A_In(A0), .B_In(B0), .Sum_Out(S0), .Carry_Out(n1_bit_full_adder_4_carry_out));
endmodule

// 1-Bit Full\nAdder
module _1_bit_full_adder (
  input  Carry_In,
  input  A_In,
  input  B_In,
  output Sum_Out,
  output Carry_Out
);

  wire n1_bit_half_adder_1_carry_out, n1_bit_half_adder_1_sum_out, n1_bit_half_adder_2_carry_out;

  _1_bit_half_adder u_1_bit_half_adder_1 (
    .A_In(A_In), .B_In(B_In), .Sum_Out(n1_bit_half_adder_1_sum_out), .Carry_Out(n1_bit_half_adder_1_carry_out));
  _1_bit_half_adder u_1_bit_half_adder_2 (
    .A_In(Carry_In), .B_In(n1_bit_half_adder_1_sum_out), .Sum_Out(Sum_Out),
    .Carry_Out(n1_bit_half_adder_2_carry_out));
  or or_1 (Carry_Out, n1_bit_half_adder_2_carry_out, n1_bit_half_adder_1_carry_out);
endmodule

module _4_bit_substractor (
  input  B3,
  input  B2,
  input  B1,
  input  B0,
  input  Invert,
  input  A3,
  input  A2,
  input  A1,
  input  A0,
  output S3,
  output S2,
  output S1,
  output S0,
  output Overflow___Underflow
);

  wire n1_bit_full_adder_1_carry_out, n1_bit_full_adder_2_carry_out, n1_bit_full_adder_3_carry_out,
       n1_bit_full_adder_4_carry_out, ones_complement_1_o0, ones_complement_1_o1, ones_complement_1_o2,
       ones_complement_1_o3;

  xor xor_1 (Overflow___Underflow, Invert, n1_bit_full_adder_1_carry_out);
  _1_bit_full_adder u_1_bit_full_adder_1 (
    .Carry_In(n1_bit_full_adder_2_carry_out), .A_In(A3), .B_In(ones_complement_1_o3), .Sum_Out(S3),
    .Carry_Out(n1_bit_full_adder_1_carry_out));
  ones_complement ones_complement_1 (
    .I3(B3), .I2(B2), .I1(B1), .I0(B0), .O3(ones_complement_1_o3), .O2(ones_complement_1_o2),
    .O1(ones_complement_1_o1), .O0(ones_complement_1_o0), .Invert(Invert));
  _1_bit_full_adder u_1_bit_full_adder_2 (
    .Carry_In(n1_bit_full_adder_3_carry_out), .A_In(A2), .B_In(ones_complement_1_o2), .Sum_Out(S2),
    .Carry_Out(n1_bit_full_adder_2_carry_out));
  _1_bit_full_adder u_1_bit_full_adder_3 (
    .Carry_In(n1_bit_full_adder_4_carry_out), .A_In(A1), .B_In(ones_complement_1_o1), .Sum_Out(S1),
    .Carry_Out(n1_bit_full_adder_3_carry_out));
  _1_bit_full_adder u_1_bit_full_adder_4 (
    .Carry_In(Invert), .A_In(A0), .B_In(ones_complement_1_o0), .Sum_Out(S0),
    .Carry_Out(n1_bit_full_adder_4_carry_out));

  // Notes on the sheet:
  //   Carry In
endmodule

// 4- Bit One's Complement
module ones_complement (
  input  I3,
  input  I2,
  input  I1,
  input  I0,
  input  Invert,
  output O3,
  output O2,
  output O1,
  output O0
);

  xor xor_1 (O3, Invert, I3);
  xor xor_2 (O2, Invert, I2);
  xor xor_3 (O1, Invert, I1);
  xor xor_4 (O0, Invert, I0);
endmodule

module _4_bit_increment (
  input  in_1,
  input  in_2,
  input  in_3,
  input  in_4,
  output out_5,
  output out_6,
  output out_7,
  output out_8,
  output out_9
);

  wire n1_bit_half_adder_2_carry_out, n1_bit_half_adder_3_carry_out, n1_bit_half_adder_4_carry_out;

  _1_bit_half_adder u_1_bit_half_adder_1 (
    .A_In(n1_bit_half_adder_2_carry_out), .B_In(in_1), .Sum_Out(out_6), .Carry_Out(out_5));
  _1_bit_half_adder u_1_bit_half_adder_2 (
    .A_In(n1_bit_half_adder_3_carry_out), .B_In(in_2), .Sum_Out(out_7),
    .Carry_Out(n1_bit_half_adder_2_carry_out));
  _1_bit_half_adder u_1_bit_half_adder_3 (
    .A_In(n1_bit_half_adder_4_carry_out), .B_In(in_3), .Sum_Out(out_8),
    .Carry_Out(n1_bit_half_adder_3_carry_out));
  _1_bit_half_adder u_1_bit_half_adder_4 (
    .A_In(1'b1), .B_In(in_4), .Sum_Out(out_9), .Carry_Out(n1_bit_half_adder_4_carry_out));
endmodule

module _4_bit_decrementer (
  input  A3,
  input  A2,
  input  A1,
  input  A0,
  input  B3,
  input  B2,
  input  B1,
  input  B0,
  output Carry_Out,
  output S3,
  output S2,
  output S1,
  output S0
);

  wire n1_bit_full_adder_2_carry_out, n1_bit_full_adder_3_carry_out, n1_bit_full_adder_4_carry_out;

  _1_bit_full_adder u_1_bit_full_adder_1 (
    .Carry_In(n1_bit_full_adder_2_carry_out), .A_In(A3), .B_In(B3), .Sum_Out(S3), .Carry_Out(Carry_Out));
  _1_bit_full_adder u_1_bit_full_adder_2 (
    .Carry_In(n1_bit_full_adder_3_carry_out), .A_In(A2), .B_In(B2), .Sum_Out(S2),
    .Carry_Out(n1_bit_full_adder_2_carry_out));
  _1_bit_full_adder u_1_bit_full_adder_3 (
    .Carry_In(n1_bit_full_adder_4_carry_out), .A_In(A1), .B_In(B1), .Sum_Out(S1),
    .Carry_Out(n1_bit_full_adder_3_carry_out));
  _1_bit_full_adder u_1_bit_full_adder_4 (
    .Carry_In(1'b0), .A_In(A0), .B_In(B0), .Sum_Out(S0), .Carry_Out(n1_bit_full_adder_4_carry_out));
endmodule
